# Fritzing sketch esp32_doorbell_silent (saved by Fritzing 0.9.3b)

parts:
  M1 = DOIT Esp32 DevKit v1 (30 pins long, 11 pins width) [part_number=ESP32S-PIN30]
  doorbell_switch_(long_phone_wire) = Pushbutton [package=THT]
  R1 = Resistor [tolerance=±5% resistance=1k package="0805 [SMD]"]
  PIR_HC-SR501 = HC-SR501 Body Sensor Module
  LED1 = LED - 3mm [color="Red (633nm)" package="3 mm [THT]"]
  R2 = Resistor [tolerance=±5% resistance=220 package="0805 [SMD]"]

nets:
  GND: M1.GND, R1.Pin_0, PIR_HC-SR501.GND, R2.Pin_0
  N1: M1.D32, LED1.anode
  N2: M1.D26, doorbell_switch_(long_phone_wire).leg1, R1.Pin_1
  N3: M1.D27, PIR_HC-SR501.OUT
  VIN: M1.VIN, doorbell_switch_(long_phone_wire).leg0, PIR_HC-SR501.VCC
  N4: LED1.cathode, R2.Pin_1

custom parts:
  DOIT Esp32 DevKit v1 (30 pins long, 11 pins width): The DOIT Esp32 DevKit v1 is one of the development board created by DOIT to evaluate the ESP-WROOM-32 module. It is based on the ESP32 microcontroller that boasts Wifi, Bluetooth, Ethernet and Low Power support all in a single chip. (vanepp) made breadboard work, adjusted pin numbering and labels and reduced size of schematic and cleaned up pcb. This chip is 30pins long (2 x15) and 11 pins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
  HC-SR501 Body Sensor Module: Pyroelectric Infrared PIR Motion Sensor Detector Module
